// Logisim project ULA4_core.circ as structural Verilog: 3 circuits, main circuit main
module main (
  input  [3:0] in_1,
  input  in_2,
  input  [3:0] in_3,
  input  in_4,
  input  [3:0] in_5,
  input  in_6,
  output [7:0] out_7
);
endmodule

module my_xor (
  input  A,
  input  B,
  output F
);

  wire and_1_out, and_2_out, not_1_out, not_2_out;

  not not_1 (not_1_out, A);
  not not_2 (not_2_out, B);
  and and_1 (and_1_out, A, not_2_out);
  and and_2 (and_2_out, not_1_out, B);
  or or_1 (F, and_1_out, and_2_out);
endmodule

module bin2gray4 (
  input  [3:0] A,
  output [3:0] F
);

  my_xor my_xor_1 (.A(A[1]), .B(A[0]), .F(F[0]));
  my_xor my_xor_2 (.A(A[2]), .B(A[1]), .F(F[1]));
  my_xor my_xor_3 (.A(A[3]), .B(A[2]), .F(F[2]));

  assign F[3] = A[3];
endmodule
